// Logisim project arch.circ as structural Verilog: 3 circuits, main circuit main
module main (
  input  EN_RAM,
  input  EN_PC,
  input  LD_PC,
  input  CLR,
  input  in_5
);

  wire CLK_out, not_1_out;
  wire [3:0] multiplexer_1_out, pc_2_1_pc1, pc_2_1_pc2;
  wire [7:0] controlled_buffer_1_out, INST1, INST2, ram_1_dout;

  Clock CLK (.out(CLK_out));
  PC_2 pc_2_1 (.EN_PC(EN_PC), .LD_PC(LD_PC), .CLK(CLK_out), .CLR(CLR), .PC1(pc_2_1_pc1), .PC2(pc_2_1_pc2));
  // Probe on multiplexer_1_out
  Multiplexer #(.width(4)) multiplexer_1 (.in0(pc_2_1_pc1), .in1(pc_2_1_pc2), .out(multiplexer_1_out), .sel(not_1_out));
  not not_1 (not_1_out, CLK_out);
  RAM #(.addrWidth(4), .enables("line")) ram_1 (.addr(multiplexer_1_out), .dout(ram_1_dout));  // open: we, clk, din
  Register #(.trigger("falling")) register_1 (.D(INST1), .en(in_5), .clk(CLK_out));  // open: Q, clr
  Register register_2 (.D(INST2), .en(in_5), .clk(CLK_out));  // open: Q, clr
  // Probe on ram_1_dout
  assign controlled_buffer_1_out = EN_RAM ? ram_1_dout : 8'bz;  // Controlled_Buffer controlled_buffer_1
  Demultiplexer #(.width(8)) demultiplexer_1 (
    .out0(INST1), .out1(INST2), .in(controlled_buffer_1_out), .sel(not_1_out));
endmodule

module PC (
  input  LD_PC,
  input  CLR,
  output [3:0] PC0,
  output [3:0] PC1
);

  wire clock_1_out;
  wire [3:0] adder_1_out, adder_2_out, multiplexer_1_out, multiplexer_2_out;

  Clock clock_1 (.out(clock_1_out));
  D_Flip_Flop d_ff_1 (.clk(clock_1_out), .preset(clock_1_out), .reset(CLR));  // open: D, Q, Qn
  Multiplexer #(.width(4)) multiplexer_1 (.in0(4'b0000), .in1(adder_1_out), .out(multiplexer_1_out), .sel(LD_PC));
  Multiplexer #(.width(4)) multiplexer_2 (.in0(4'b0001), .in1(adder_2_out), .out(multiplexer_2_out), .sel(LD_PC));
  Counter #(.max('hf), .ongoal("stay"), .width(4)) counter_1 (
    .load(1'b1), .D(multiplexer_1_out), .Q(PC0), .clk(clock_1_out), .clr(CLR));  // open: count, carry, up
  Counter #(.max('hf), .ongoal("stay"), .width(4)) counter_2 (
    .load(1'b1), .D(multiplexer_2_out), .Q(PC1), .clk(clock_1_out), .clr(CLR));  // open: count, carry, up
  Adder #(.width(4)) adder_1 (.a(4'b0010), .b(PC0), .out(adder_1_out));  // open: cin, cout
  Adder #(.width(4)) adder_2 (.a(4'b0010), .b(PC1), .out(adder_2_out));  // open: cin, cout
endmodule

module PC_2 (
  input  EN_PC,
  input  LD_PC,
  input  CLK,
  input  CLR,
  output [3:0] PC1,
  output [3:0] PC2
);

  wire not_1_out;
  wire [2:0] counter_1_q, counter_2_q;
  wire [3:0] rom_1_data, rom_2_data;

  not not_1 (not_1_out, LD_PC);
  ROM #(.addrWidth(3), .dataWidth(4)) rom_1 (.addr(counter_1_q), .data(rom_1_data));
  Counter #(.max('h7), .width(3)) counter_1 (
    .load(not_1_out), .D(counter_1_q), .Q(counter_1_q), .clk(CLK), .clr(CLR));  // open: count, carry, up
  Counter #(.max('h7), .trigger("falling"), .width(3)) counter_2 (
    .load(not_1_out), .D(counter_2_q), .Q(counter_2_q), .clk(CLK), .clr(CLR));  // open: count, carry, up
  ROM #(.addrWidth(3), .dataWidth(4)) rom_2 (.addr(counter_2_q), .data(rom_2_data));
  assign PC1 = EN_PC ? rom_1_data : 4'bz;  // Controlled_Buffer controlled_buffer_1
  assign PC2 = EN_PC ? rom_2_data : 4'bz;  // Controlled_Buffer controlled_buffer_2

  // Notes on the sheet:
  //   contents of rom_1 (hex, n*v repeats v):
  //   0 2 4 8 a c e
  //   contents of rom_2 (hex, n*v repeats v):
  //   1 3 5 7 9 b d f
endmodule
